# Fritzing sketch dpSniffino_shematic (saved by Fritzing 0.9.3b)
circuit board: 9.5cm x 5.60421cm
stripboards: 1

parts:
  U2 = ENC28J60 Breakout Board
  U1 = Arduino Pro Mini v13  # not connected
  UP = Pushbutton [package="[THT]"]
  R3 = Resistor [tolerance=±5% resistance=10k package=THT]
  R2 = Resistor [tolerance=±5% resistance=10k package=THT]
  R1 = Resistor [tolerance=±5% resistance=10k package=THT]
  R4 = Resistor [tolerance=±5% resistance=10k package=THT]
  DOWN = Pushbutton [package="[THT]"]
  LEFT = Pushbutton [package="[THT]"]
  RIGHT = Pushbutton [package="[THT]"]
  LCD1 = LCD screen
  R6 = Trimmer Potentiometer [maximum_resistance=10kΩ package=THT]
  J1 = female pin header, 16 pins [form="♀ (female)"]
  S5 = Toggle Switch [package=THT]
  J11 = double row male pin header, 2 pins [form="♂ (male)"]
  J14 = male pin header, 16 pins [form="♂ (male)"]
  J12 = male pin header, 5 pins [form="♂ (male)"]
  J13 = male pin header, 5 pins [form="♂ (male)"]
  VCC1 = Battery block 9V
  J15 = female pin header, 2 pins [form="♀ (female)"]
  J10 = female pin header, 3 pins [form="♀ (female)"]
  J2 = female pin header, 12 pins [form="♀ (female)"]
  J3 = female pin header, 12 pins [form="♀ (female)"]
  J4 = female pin header, 4 pins [form="♀ (female)"]
  J5 = female pin header, 4 pins [form="♀ (female)"]
  J6 = female pin header, 4 pins [form="♀ (female)"]
  J16 = male pin header, 1 pin [form="♂ (male)"]
  J17 = male pin header, 1 pin [form="♂ (male)"]
  J18 = male pin header, 1 pin [form="♂ (male)"]
  J19 = male pin header, 1 pin [form="♂ (male)"]
  J9 = female pin header, 3 pins [form="♀ (female)"]
  R5 = Resistor [tolerance=±5% resistance=220 package=THT]
  J8 = female pin header, 4 pins [form="♀ (female)"]
  J7 = female pin header, 3 pins [form="♀ (female)"]
  J20 = male pin header, 3 pins [form="♂ (male)"]
  R7 = Resistor [tolerance=±5% resistance=100k package=THT]
  J21 = female pin header, 2 pins [form="♀ (female)"]
  J22 = female pin header, 2 pins [form="♀ (female)"]
  J23 = female pin header, 2 pins [form="♀ (female)"]
  J24 = female pin header, 2 pins [form="♀ (female)"]
  J25 = female pin header, 3 pins [form="♀ (female)"]

nets:
  N1: U2.VCC, J12.pin1
  N2: U2.GND, J13.pin1
  N3: U2.RESET, J13.pin2
  N4: U2.CS, J12.pin2
  N5: U2.SI, J12.pin3
  N6: U2.SCK, J13.pin3
  N7: U2.WOL, J12.pin4
  N8: U2.SO, J13.pin4
  N9: U2.INT, J13.pin5
  N10: U2.CLKOUT, J12.pin5
  D6: UP.Pin_1, UP.Pin_2, R1.Pin_1, J2.pin4, J21.pin1
  GND: UP.Pin_3, UP.Pin_4, DOWN.Pin_3, DOWN.Pin_4, LEFT.Pin_3, LEFT.Pin_4, RIGHT.Pin_3, RIGHT.Pin_4, R6.leg2, J1.pin1, J1.pin5, J1.pin16, J11.pin2, J10.pin1, J2.pin9, J3.pin11, J9.pin1, J8.pin1, J21.pin2, J22.pin2, J23.pin2, J24.pin2
  VCC: R3.Pin_0, R2.Pin_0, R1.Pin_0, R4.Pin_0, R6.leg1, J1.pin2, J3.pin9, R5.Pin_0
  D8: R3.Pin_1, LEFT.Pin_1, LEFT.Pin_2, J2.pin2, J23.pin1
  D7: R2.Pin_1, DOWN.Pin_1, DOWN.Pin_2, J2.pin3, J22.pin1
  D9: R4.Pin_1, RIGHT.Pin_1, RIGHT.Pin_2, J2.pin1, J24.pin1
  N11: LCD1.VSS, J14.pin1
  N12: LCD1.VDD, J14.pin2
  N13: LCD1.V0, J14.pin3
  N14: LCD1.RS, J14.pin4
  N15: LCD1.R/W, J14.pin5
  N16: LCD1.E, J14.pin6
  N17: LCD1.DB0, J14.pin7
  N18: LCD1.DB1, J14.pin8
  N19: LCD1.DB2, J14.pin9
  N20: LCD1.DB3, J14.pin10
  N21: LCD1.DB4, J14.pin11
  N22: LCD1.DB5, J14.pin12
  N23: LCD1.DB6, J14.pin13
  N24: LCD1.DB7, J14.pin14
  N25: LCD1.LED+, J14.pin15
  N26: LCD1.LED-, J14.pin16
  N27: R6.wiper, J1.pin3
  D5: J1.pin4, J2.pin5
  D4: J1.pin6, J2.pin6
  D3: J1.pin11, J2.pin7
  D2: J1.pin12, J2.pin8
  N28: J1.pin13, J5.pin1, J5.pin2, J5.pin3, J5.pin4
  N29: J1.pin14, J6.pin1, J6.pin2, J6.pin3, J6.pin4
  N30: J1.pin15, R5.Pin_1
  N31: S5.L1, J25.pin1
  N32: S5.COM, J25.pin2
  N33: S5.L2, J25.pin3
  N34: J11.pin1, J20.pin3
  N35: VCC1.-, J15.pin2
  N36: VCC1.+, J15.pin1
  3.3V: J10.pin2, J7.pin1
  RAW: J10.pin3, J3.pin12, J9.pin2
  RST': J2.pin10
  RXI: J2.pin11
  TXO: J2.pin12
  D10: J3.pin1, J7.pin2
  D11: J3.pin2, J7.pin3
  D12: J3.pin3, J8.pin4
  D13: J3.pin4, J8.pin3
  A0: J3.pin5, J4.pin1
  A1: J3.pin6, J4.pin2
  N37: J3.pin7, R7.Pin_1
  A3: J3.pin8, J4.pin4
  RST: J3.pin10, J8.pin2
  A2: J4.pin3, R7.Pin_0
  N38: J16.pin1, J17.pin1
  N39: J18.pin1, J19.pin1
  N40: J9.pin3, J20.pin1, J20.pin2

notes:
  D10
  D11
  D12
  D13
  CS
  SI
  SO
  SCK
  RST
  3.3V
  GND
  9v_I
  5v_I
  3.3v_O
  9V
  5V
  dpSniffino, 0.5
  A0
  RAW
  VCC
  A1
  A2
  A3
  --Raw-LCD--
  --Vcc-LCD--
  --NIC-D10--
  --NIC-D8--
  WOL
  CLK
  INT
  RESET
  3.3v
  5v
  9v
  dpSniffino v0.5

custom parts:
  ENC28J60 Breakout Board: This is a breakout board for the Microchip ENC28J60 stand-alone ethernet controller. The ENC28J60 has an SPI interface. It operates at 3.3 Volts.
